# Fritzing sketch Smart Home Security System (saved by Fritzing 0.9.2b)
breadboards: 1

parts:
  Part1 = Arduino Mega 2560 (Rev3)
  U1 = MLX90614 [package=to-39]
  U2 = MLX90614 [package=to-39]
  U3 = LCD-16X2 [package=lcd-8x2-kit]
  LED1 = LEDs [package=led10mm]
  LED2 = LEDs [package=led10mm]
  J1 = Basic Servo
  J2 = Infrared Proximity Sensor
  J3 = Infrared Proximity Sensor  # not connected
  J4 = Piezo Speaker

nets:
  N1: Part1.D21/SCL, U3.DB3
  N2: Part1.D20/SDA, U3.DB1
  N3: Part1.D12_PWM, J1.vcc
  N4: Part1.D8_PWM, J2.Vout
  5V: Part1.5V, J1.pulse, J2.Vcc
  GND: Part1.GND, Part1.D30, Part1.D32, LED1.A, LED1.C, LED2.A, LED2.C, J1.gnd, J2.GND, J4.pin1
  N5: Part1.D2_PWM, U1.SCL_VZ
  N6: Part1.D22, J4.pin2
  N7: Part1.D34, U2.SCL_VZ, U2.PWM_SDA
